// Logisim project 150115013_150115032.circ as structural Verilog: 8 circuits, main circuit main
module main (
  output [15:0] out_1,
  output out_2
);

  wire button_1_out, button_2_out, button_3_out, button_4_out, clock_1_out, cpu_1_cf, cpu_1_zf;

  Button button_1 (.out(button_1_out));
  Button button_2 (.out(button_2_out));
  CPU cpu_1 (
    .carry_out(out_2), .ZF(cpu_1_zf), .CF(cpu_1_cf), .Reset_Flags(button_4_out), .in_3(button_2_out),
    .in_2(button_1_out), .in_4(button_3_out), .out_6(out_1), .clock(clock_1_out));
  Button button_3 (.out(button_3_out));
  Clock clock_1 (.out(clock_1_out));
  Button button_4 (.out(button_4_out));
  LED led_1 (.in(cpu_1_zf));
  LED led_2 (.in(cpu_1_cf));
endmodule

module _1_bit_ALU (
  input  input_1,
  input  input_2,
  input  carry_in,
  input  operation,
  output result,
  output carry_out
);

  wire adder_1_out, and_1_out;

  and and_1 (and_1_out, input_1, input_2);
  Adder #(.width(1)) adder_1 (.a(input_1), .b(input_2), .out(adder_1_out), .cin(carry_in), .cout(carry_out));
  Multiplexer multiplexer_1 (.in0(and_1_out), .in1(adder_1_out), .out(result), .sel(operation));  // open: en
endmodule

// ALU
module _16_bit_ALU (
  input  operation,
  input  [15:0] input_1,
  input  [15:0] input_2,
  output [15:0] result,
  output carry_out
);

  wire carry_out_8, n1_bit_alu_1_carry_out, n1_bit_alu_2_carry_out, n1_bit_alu_3_carry_out,
       n1_bit_alu_4_carry_out, n1_bit_alu_5_carry_out, n1_bit_alu_6_carry_out, n1_bit_alu_7_carry_out,
       n1_bit_alu_9_carry_out, n1_bit_alu_10_carry_out, n1_bit_alu_11_carry_out, n1_bit_alu_12_carry_out,
       n1_bit_alu_13_carry_out, n1_bit_alu_14_carry_out, n1_bit_alu_15_carry_out;

  // Probe on result
  // Probe on input_1
  // Probe on input_2
  _1_bit_ALU u_1_bit_alu_1 (
    .input_1(input_1[0]), .input_2(input_2[0]), .result(result[0]), .carry_in(1'b0),
    .carry_out(n1_bit_alu_1_carry_out), .operation(operation));
  _1_bit_ALU u_1_bit_alu_2 (
    .input_1(input_1[1]), .input_2(input_2[1]), .result(result[1]), .carry_in(n1_bit_alu_1_carry_out),
    .carry_out(n1_bit_alu_2_carry_out), .operation(operation));
  _1_bit_ALU u_1_bit_alu_3 (
    .input_1(input_1[2]), .input_2(input_2[2]), .result(result[2]), .carry_in(n1_bit_alu_2_carry_out),
    .carry_out(n1_bit_alu_3_carry_out), .operation(operation));
  _1_bit_ALU u_1_bit_alu_4 (
    .input_1(input_1[3]), .input_2(input_2[3]), .result(result[3]), .carry_in(n1_bit_alu_3_carry_out),
    .carry_out(n1_bit_alu_4_carry_out), .operation(operation));
  _1_bit_ALU u_1_bit_alu_5 (
    .input_1(input_1[4]), .input_2(input_2[4]), .result(result[4]), .carry_in(n1_bit_alu_4_carry_out),
    .carry_out(n1_bit_alu_5_carry_out), .operation(operation));
  _1_bit_ALU u_1_bit_alu_6 (
    .input_1(input_1[5]), .input_2(input_2[5]), .result(result[5]), .carry_in(n1_bit_alu_5_carry_out),
    .carry_out(n1_bit_alu_6_carry_out), .operation(operation));
  _1_bit_ALU u_1_bit_alu_7 (
    .input_1(input_1[6]), .input_2(input_2[6]), .result(result[6]), .carry_in(n1_bit_alu_6_carry_out),
    .carry_out(n1_bit_alu_7_carry_out), .operation(operation));
  _1_bit_ALU u_1_bit_alu_8 (
    .input_1(input_1[7]), .input_2(input_2[7]), .result(result[7]), .carry_in(n1_bit_alu_7_carry_out),
    .carry_out(carry_out_8), .operation(operation));
  _1_bit_ALU u_1_bit_alu_9 (
    .input_1(input_1[8]), .input_2(input_2[8]), .result(result[8]), .carry_in(carry_out_8),
    .carry_out(n1_bit_alu_9_carry_out), .operation(operation));
  _1_bit_ALU u_1_bit_alu_10 (
    .input_1(input_1[9]), .input_2(input_2[9]), .result(result[9]), .carry_in(n1_bit_alu_9_carry_out),
    .carry_out(n1_bit_alu_10_carry_out), .operation(operation));
  _1_bit_ALU u_1_bit_alu_11 (
    .input_1(input_1[10]), .input_2(input_2[10]), .result(result[10]), .carry_in(n1_bit_alu_10_carry_out),
    .carry_out(n1_bit_alu_11_carry_out), .operation(operation));
  _1_bit_ALU u_1_bit_alu_12 (
    .input_1(input_1[11]), .input_2(input_2[11]), .result(result[11]), .carry_in(n1_bit_alu_11_carry_out),
    .carry_out(n1_bit_alu_12_carry_out), .operation(operation));
  _1_bit_ALU u_1_bit_alu_13 (
    .input_1(input_1[12]), .input_2(input_2[12]), .result(result[12]), .carry_in(n1_bit_alu_12_carry_out),
    .carry_out(n1_bit_alu_13_carry_out), .operation(operation));
  _1_bit_ALU u_1_bit_alu_14 (
    .input_1(input_1[13]), .input_2(input_2[13]), .result(result[13]), .carry_in(n1_bit_alu_13_carry_out),
    .carry_out(n1_bit_alu_14_carry_out), .operation(operation));
  _1_bit_ALU u_1_bit_alu_15 (
    .input_1(input_1[14]), .input_2(input_2[14]), .result(result[14]), .carry_in(n1_bit_alu_14_carry_out),
    .carry_out(n1_bit_alu_15_carry_out), .operation(operation));
  _1_bit_ALU u_1_bit_alu_16 (
    .input_1(input_1[15]), .input_2(input_2[15]), .result(result[15]), .carry_in(n1_bit_alu_15_carry_out),
    .carry_out(carry_out), .operation(operation));

  // Other names for the same wires on the sheet: in1_last8[7:0] = input_1[15:8]; in2_last8[7:0] = input_2[15:8];
  //   output[15:0] = result
endmodule

module Register_file (
  input  [15:0] data,
  input  [3:0] Write_Register,
  input  [3:0] Read_Register_1,
  input  [3:0] Read_Register_2,
  input  regWrite,
  input  clock,
  input  clear,
  output [15:0] Reg_Data_1,
  output [15:0] Reg_Data_2
);

  wire and_1_out, and_2_out, and_3_out, and_4_out, and_5_out, and_6_out, and_7_out, and_8_out, and_9_out,
       and_10_out, and_11_out, and_12_out, and_13_out, and_14_out, and_15_out, and_16_out, decoder_1_out0,
       decoder_1_out1, decoder_1_out2, decoder_1_out3, decoder_1_out4, decoder_1_out5, decoder_1_out6,
       decoder_1_out7, decoder_1_out8, decoder_1_out9, decoder_1_out10, decoder_1_out11, decoder_1_out12,
       decoder_1_out13, decoder_1_out14, decoder_1_out15;
  wire [15:0] R0_q, R1_q, R2_q, R3_q, R4_q, R5_q, R6_q, R7_q, R8_q, R9_q, R10_q, R11_q, R12_q, R13_q, R14_q,
       R15_q;

  Decoder #(.select(4)) decoder_1 (
    .out0(decoder_1_out0), .out1(decoder_1_out1), .out2(decoder_1_out2), .out3(decoder_1_out3),
    .out4(decoder_1_out4), .out5(decoder_1_out5), .out6(decoder_1_out6), .out7(decoder_1_out7),
    .out8(decoder_1_out8), .out9(decoder_1_out9), .out10(decoder_1_out10), .out11(decoder_1_out11),
    .out12(decoder_1_out12), .out13(decoder_1_out13), .out14(decoder_1_out14), .out15(decoder_1_out15),
    .sel(Write_Register));  // open: en
  // Probe on data
  and and_1 (and_1_out, decoder_1_out0, regWrite);
  and and_2 (and_2_out, decoder_1_out1, regWrite);
  and and_3 (and_3_out, decoder_1_out2, regWrite);
  and and_4 (and_4_out, decoder_1_out3, regWrite);
  and and_5 (and_5_out, decoder_1_out4, regWrite);
  and and_6 (and_6_out, decoder_1_out5, regWrite);
  and and_7 (and_7_out, decoder_1_out6, regWrite);
  and and_8 (and_8_out, decoder_1_out7, regWrite);
  Register #(.width(16)) R0 (.D(data), .en(and_1_out), .Q(R0_q), .clk(clock), .clr(clear));
  Register #(.width(16)) R1 (.D(data), .en(and_2_out), .Q(R1_q), .clk(clock), .clr(clear));
  Register #(.width(16)) R2 (.D(data), .en(and_3_out), .Q(R2_q), .clk(clock), .clr(clear));
  Register #(.width(16)) R3 (.D(data), .en(and_4_out), .Q(R3_q), .clk(clock), .clr(clear));
  Register #(.width(16)) R4 (.D(data), .en(and_5_out), .Q(R4_q), .clk(clock), .clr(clear));
  Register #(.width(16)) R5 (.D(data), .en(and_6_out), .Q(R5_q), .clk(clock), .clr(clear));
  Register #(.width(16)) R6 (.D(data), .en(and_7_out), .Q(R6_q), .clk(clock), .clr(clear));
  Register #(.width(16)) R7 (.D(data), .en(and_8_out), .Q(R7_q), .clk(clock), .clr(clear));
  and and_9 (and_9_out, decoder_1_out8, regWrite);
  and and_10 (and_10_out, decoder_1_out9, regWrite);
  and and_11 (and_11_out, decoder_1_out10, regWrite);
  and and_12 (and_12_out, decoder_1_out11, regWrite);
  and and_13 (and_13_out, decoder_1_out12, regWrite);
  and and_14 (and_14_out, decoder_1_out13, regWrite);
  and and_15 (and_15_out, decoder_1_out14, regWrite);
  and and_16 (and_16_out, decoder_1_out15, regWrite);
  Register #(.width(16)) R8 (.D(data), .en(and_9_out), .Q(R8_q), .clk(clock), .clr(clear));
  Register #(.width(16)) R9 (.D(data), .en(and_10_out), .Q(R9_q), .clk(clock), .clr(clear));
  Register #(.width(16)) R10 (.D(data), .en(and_11_out), .Q(R10_q), .clk(clock), .clr(clear));
  Register #(.width(16)) R11 (.D(data), .en(and_12_out), .Q(R11_q), .clk(clock), .clr(clear));
  Register #(.width(16)) R12 (.D(data), .en(and_13_out), .Q(R12_q), .clk(clock), .clr(clear));
  Register #(.width(16)) R13 (.D(data), .en(and_14_out), .Q(R13_q), .clk(clock), .clr(clear));
  Register #(.width(16)) R14 (.D(data), .en(and_15_out), .Q(R14_q), .clk(clock), .clr(clear));
  Register #(.width(16)) R15 (.D(data), .en(and_16_out), .Q(R15_q), .clk(clock), .clr(clear));
  Multiplexer #(.select(4), .width(16)) multiplexer_1 (
    .in0(R0_q), .in1(R1_q), .in2(R2_q), .in3(R3_q), .in4(R4_q), .in5(R5_q), .in6(R6_q), .in7(R7_q),
    .in8(R8_q), .in9(R9_q), .in10(R10_q), .in11(R11_q), .in12(R12_q), .in13(R13_q), .in14(R14_q),
    .in15(R15_q), .out(Reg_Data_1), .sel(Read_Register_1));  // open: en
  // Probe on Reg_Data_1
  Multiplexer #(.select(4), .width(16)) multiplexer_2 (
    .in0(R0_q), .in1(R1_q), .in2(R2_q), .in3(R3_q), .in4(R4_q), .in5(R5_q), .in6(R6_q), .in7(R7_q),
    .in8(R8_q), .in9(R9_q), .in10(R10_q), .in11(R11_q), .in12(R12_q), .in13(R13_q), .in14(R14_q),
    .in15(R15_q), .out(Reg_Data_2), .sel(Read_Register_2));  // open: en
  // Probe on Reg_Data_2
endmodule

module CPU (
  input  clock,
  input  in_2,
  input  in_3,
  input  in_4,
  input  Reset_Flags,
  output [15:0] out_6,
  output ZF,
  output CF,
  output carry_out
);

  wire ALUControl, COMPSignal, IMMSignal, InstRead, JUMPSig, MemLoad, MemStore, not_1_out, PCRead, WriteReg;
  wire [3:0] DEST, multiplexer_2_out, multiplexer_3_out, OP1, OP2, SRC1, SRC2;
  wire [11:0] JUMP_ADDR, LD_ST_ADDR, pc_register_1_pc_address;
  wire [15:0] ALU_Result, DataMemVal, IMM, multiplexer_1_out, multiplexer_4_out, OP1Vaue, OP2Value, REG1Out,
       REG2Out, register_file_1_reg_data_1, register_file_1_reg_data_2, rom_1_data;

  PC_Register pc_register_1 (
    .JUMP_ADDRESS(JUMP_ADDR), .ADDRSelect(JUMPSig), .PC_address(pc_register_1_pc_address), .Enable(PCRead),
    .Clock(clock), .Clear(in_3));
  Control_unit control_unit_1 (
    .operand1(OP1Vaue), .operand2(OP2Value), .ALU_SIGNAL(ALUControl), .MEM_LOAD(MemLoad),
    .JUMP_SIGNAL(JUMPSig), .REG_WRITE(WriteReg), .IMM_SIGNAL(IMMSignal), .MEM_STORE(MemStore),
    .PCRead(PCRead), .INSTRead(InstRead), .instruction(out_6), .JUMP_ADDR(JUMP_ADDR), .SRC1(SRC1),
    .SRC2(SRC2), .LD_ST_ADDR(LD_ST_ADDR), .OP1(OP1), .OP2(OP2), .DEST(DEST), .IMM(IMM), .Compare(COMPSignal),
    .ZF(ZF), .CF(CF), .Reset_Flags(Reset_Flags), .clock(clock));
  // Probe on pc_register_1_pc_address
  ROM #(.addrWidth(12), .dataWidth(16)) rom_1 (.addr(pc_register_1_pc_address), .data(rom_1_data));  // open: sel
  // Probe on rom_1_data
  Register #(.width(16)) Instruction_Register (.D(rom_1_data), .en(InstRead), .Q(out_6), .clk(clock), .clr(in_2));
  not not_1 (not_1_out, MemLoad);
  Multiplexer #(.width(16)) multiplexer_1 (
    .in0(DataMemVal), .in1(ALU_Result), .out(multiplexer_1_out), .sel(not_1_out));  // open: en
  Multiplexer #(.width(4)) multiplexer_2 (
    .in0(SRC1), .in1(OP1), .out(multiplexer_2_out), .sel(COMPSignal));  // open: en
  Multiplexer #(.width(4)) multiplexer_3 (
    .in0(SRC2), .in1(OP2), .out(multiplexer_3_out), .sel(COMPSignal));  // open: en
  Register_file register_file_1 (
    .data(multiplexer_1_out), .Read_Register_1(multiplexer_2_out), .Read_Register_2(multiplexer_3_out),
    .Reg_Data_1(register_file_1_reg_data_1), .Reg_Data_2(register_file_1_reg_data_2), .Write_Register(DEST),
    .regWrite(WriteReg), .clock(clock), .clear(in_4));
  _16balu u_16balu_1 (
    .A(REG1Out), .B(multiplexer_4_out), .Result(ALU_Result), .Operation(ALUControl), .Carry_out(carry_out));
  Multiplexer #(.width(16)) multiplexer_4 (
    .in0(REG2Out), .in1(IMM), .out(multiplexer_4_out), .sel(IMMSignal));  // open: en
  // Probe on ALU_Result
  RAM #(.addrWidth(12), .dataWidth(16), .bus("separate")) ram_1 (
    .addr(LD_ST_ADDR), .din(REG1Out), .data(DataMemVal), .str(MemStore), .clk(clock), .ld(MemLoad));  // open: sel, clr
  Demultiplexer #(.width(16)) demultiplexer_1 (
    .out0(REG1Out), .out1(OP1Vaue), .in(register_file_1_reg_data_1), .sel(COMPSignal));  // open: en
  Demultiplexer #(.width(16)) demultiplexer_2 (
    .out0(REG2Out), .out1(OP2Value), .in(register_file_1_reg_data_2), .sel(COMPSignal));  // open: en

  // Other names for the same wires on the sheet: Instruction[15:0] = out_6

  // Notes on the sheet:
  //   Instruction Memory
  //   contents of rom_1 (hex, n*v repeats v):
  //   3000 3101 3202 3303 9003 2223 7331 8020 cffd 4204 722d 8021 effe 4205 5421 4406
  //   Data Memory
endmodule

module Control_unit (
  input  [15:0] instruction,
  input  clock,
  input  Reset_Flags,
  input  [15:0] operand1,
  input  [15:0] operand2,
  output [11:0] LD_ST_ADDR,
  output [3:0] DEST,
  output [11:0] JUMP_ADDR,
  output [15:0] IMM,
  output [3:0] SRC1,
  output [3:0] SRC2,
  output [3:0] OP1,
  output [3:0] OP2,
  output ALU_SIGNAL,
  output REG_WRITE,
  output JUMP_SIGNAL,
  output MEM_LOAD,
  output IMM_SIGNAL,
  output Compare,
  output MEM_STORE,
  output ZF,
  output PCRead,
  output INSTRead,
  output CF
);

  wire above, ADD, ADDI, AND, and_1_out, and_2_out, and_3_out, and_4_out, and_5_out, and_6_out, ANDI, below,
       equal, JA, JAE, JB, JBE, JE, JUMP, not_1_out, not_2_out, not_4_out, not_5_out, not_6_out, not_7_out,
       not_8_out, or_3_out;

  Decoder #(.select(4)) decoder_1 (
    .out1(AND), .out2(ADD), .out3(MEM_LOAD), .out4(MEM_STORE), .out5(ANDI), .out7(ADDI), .out8(Compare),
    .out9(JUMP), .out10(JE), .out11(JA), .out12(JB), .out13(JBE), .out14(JAE), .sel(instruction[15:12]));  // open: out0, out6, out15, en
  not not_1 (not_1_out, above);
  not not_2 (not_2_out, equal);
  Comparator #(.width(16), .mode("unsigned")) comparator_1 (
    .a(operand1), .b(operand2), .gt(above), .eq(equal), .lt(below));
  Register #(.width(1), .trigger("falling")) register_1 (
    .D(equal), .en(Compare), .Q(ZF), .clk(clock), .clr(Reset_Flags));
  Register #(.width(1), .trigger("falling")) register_2 (
    .D(and_1_out), .en(Compare), .Q(CF), .clk(clock), .clr(Reset_Flags));
  and and_1 (and_1_out, not_1_out, not_2_out);
  or or_1 (IMM_SIGNAL, ANDI, ADDI);
  not not_3 (INSTRead, clock);
  or or_2 (REG_WRITE, ANDI, ADDI, AND, ADD, MEM_LOAD);
  or or_3 (or_3_out, ZF, CF);
  Multiplexer #(.width(4)) multiplexer_1 (
    .in0(instruction[7:4]), .in1(instruction[11:8]), .out(SRC1), .sel(MEM_STORE));  // open: en
  and and_2 (and_2_out, JE, ZF, not_4_out);
  not not_4 (not_4_out, CF);
  and and_3 (and_3_out, JA, not_5_out, not_6_out);
  not not_5 (not_5_out, ZF);
  not not_6 (not_6_out, CF);
  and and_4 (and_4_out, JB, not_7_out, CF);
  not not_7 (not_7_out, ZF);
  and and_5 (and_5_out, JAE, not_8_out);
  not not_8 (not_8_out, CF);
  and and_6 (and_6_out, JBE, or_3_out);
  assign LD_ST_ADDR = {{4{1'b0}}, instruction[7:0]};  // Bit_Extender bit_extender_1
  or or_4 (JUMP_SIGNAL, JUMP, and_2_out, and_3_out, and_4_out, and_5_out, and_6_out);
  assign IMM = {{12{instruction[3]}}, instruction[3:0]};  // Bit_Extender bit_extender_2

  assign ALU_SIGNAL = instruction[13];
  assign DEST = instruction[11:8];
  assign JUMP_ADDR = instruction[11:0];
  assign OP1 = instruction[7:4];
  assign OP2 = instruction[3:0];
  assign PCRead = clock;
  assign SRC2 = instruction[3:0];

  // Other names for the same wires on the sheet: CMP = Compare; IMM_t[3:0] = instruction[3:0];
  //   LD_ST_ADDR_t[7:0] = instruction[7:0]; LD = MEM_LOAD; Opcode[3:0] = instruction[15:12];
  //   SRC1_t[3:0] = instruction[7:4]; ST = MEM_STORE
endmodule

module PC_Register (
  input  [11:0] JUMP_ADDRESS,
  input  ADDRSelect,
  input  Clear,
  input  Enable,
  input  Clock,
  output [11:0] PC_address
);

  wire [11:0] adder_1_out, multiplexer_1_out;

  Multiplexer #(.width(12)) multiplexer_1 (
    .in0(12'h1), .in1(JUMP_ADDRESS), .out(multiplexer_1_out), .sel(ADDRSelect));  // open: en
  Adder #(.width(12)) adder_1 (.a(multiplexer_1_out), .b(PC_address), .out(adder_1_out));  // open: cin, cout
  Register #(.width(12), .trigger("falling")) register_1 (
    .D(adder_1_out), .en(Enable), .Q(PC_address), .clk(Clock), .clr(Clear));
endmodule

// ALU
module _16balu (
  input  Operation,
  input  [15:0] A,
  input  [15:0] B,
  output [15:0] Result,
  output Carry_out
);

  wire [15:0] adder_1_out, and_1_out;

  assign and_1_out = A & B;  // AND_Gate and_1, 16 bits wide
  Adder #(.width(16)) adder_1 (.a(A), .b(B), .out(adder_1_out), .cin(1'b0), .cout(Carry_out));
  Multiplexer #(.width(16)) multiplexer_1 (
    .in0(and_1_out), .in1(adder_1_out), .out(Result), .sel(Operation));  // open: en
endmodule
